// Logisim project UNIVERSALSHIFTREGISTER.circ as structural Verilog: 1 circuit, main circuit main
module main (
  input  I2,
  input  I3,
  input  I0,
  input  I1,
  input  RIGHT_SHIFT,
  input  LEFT_SHIFT,
  input  [1:0] SELECTION_BITS,
  output [3:0] out_8
);

  wire clock_1_out, multiplexer_1_out, multiplexer_2_out, multiplexer_3_out, multiplexer_4_out;

  Clock clock_1 (.out(clock_1_out));
  D_Flip_Flop d_ff_1 (.D(multiplexer_1_out), .clk(clock_1_out), .Q(out_8[3]));  // open: Qn, preset, reset
  Multiplexer #(.select(2)) multiplexer_1 (
    .in0(RIGHT_SHIFT), .in1(out_8[2]), .in2(I0), .in3(out_8[3]), .out(multiplexer_1_out), .sel(SELECTION_BITS));
  Multiplexer #(.select(2)) multiplexer_2 (
    .in0(out_8[3]), .in1(out_8[1]), .in2(I1), .in3(out_8[2]), .out(multiplexer_2_out), .sel(SELECTION_BITS));
  D_Flip_Flop d_ff_2 (.D(multiplexer_2_out), .clk(clock_1_out), .Q(out_8[2]));  // open: Qn, preset, reset
  Multiplexer #(.select(2)) multiplexer_3 (
    .in0(out_8[2]), .in1(out_8[0]), .in2(I2), .in3(out_8[1]), .out(multiplexer_3_out), .sel(SELECTION_BITS));
  D_Flip_Flop d_ff_3 (.D(multiplexer_3_out), .clk(clock_1_out), .Q(out_8[1]));  // open: Qn, preset, reset
  Multiplexer #(.select(2)) multiplexer_4 (
    .in0(out_8[1]), .in1(LEFT_SHIFT), .in2(I3), .in3(out_8[0]), .out(multiplexer_4_out), .sel(SELECTION_BITS));
  D_Flip_Flop d_ff_4 (.D(multiplexer_4_out), .clk(clock_1_out), .Q(out_8[0]));  // open: Qn, preset, reset
endmodule
